# Fritzing sketch raspberry-real (saved by Fritzing 0.9.3b)
breadboards: 1

parts:
  Raspberry_Pi_1 = Raspberry Pi 3 [part_number=RPI-3-V1.2]
  hc-sr1 = hc-sr04
  F2 = Small Fan, based on Fan - Ventilador [package=THT]
  R6 = Resistor [tolerance=±1% resistance=1k package=THT]
  R7 = Resistor [tolerance=±1% resistance=1k package=THT]
  R8 = Resistor [tolerance=±1% resistance=1k package=THT]
  Q1 = TRANSISTOR_NPN [package=to-92]
  D1 = Diode [package=diode-1n4148]
  R9 = Resistor [tolerance=±2% resistance=470 package=THT]

nets:
  5V: Raspberry_Pi_1.3v3, Raspberry_Pi_1.5V, hc-sr1.VCC, F2.5V, D1.A
  GND: Raspberry_Pi_1.GPIO2, Raspberry_Pi_1.GND, hc-sr1.Echo, hc-sr1.GND, R6.Pin_1, R7.Pin_0, R8.Pin_0, Q1.E
  N1: Raspberry_Pi_1.GIPO17, hc-sr1.Trig
  N2: Raspberry_Pi_1.GIPO27, R6.Pin_0, R7.Pin_1, R8.Pin_1
  N3: Raspberry_Pi_1.GIPO22, R9.Pin_1
  N4: F2.GND, Q1.C
  N5: Q1.B, R9.Pin_0

custom parts:
  Small Fan, based on Fan - Ventilador: Small 2-pin fan, commonly used with single-board computers, 3d-printers, etc. This work is based on a much larger fan, as commonly found in desktop computers
